# Fritzing sketch schematic (saved by Fritzing 0.9.3b)

parts:
  BeagleBone = BeagleBone Black
  Current-limiting = Resistor [tolerance=±5% resistance=470 package=THT]
  Keypad = mystery part, 12 pins [chip_label=Keypad]
  Pull-down = Resistor [tolerance=±5% resistance=68k package=THT]
  Pull-down_2 = Resistor [tolerance=±5% resistance=68k package=THT]

nets:
  N1: BeagleBone.no_name_yet#106, Keypad.pin6, Pull-down.Pin_0
  N2: BeagleBone.no_name_yet#201, Pull-down.Pin_1, Pull-down_2.Pin_1
  N3: BeagleBone.no_name_yet#202, Current-limiting.Pin_1
  N4: Current-limiting.Pin_0, Keypad.pin1
  N5: Keypad.pin10, Pull-down_2.Pin_0

custom parts:
  BeagleBone Black: BeagleBone Black rev. A5B
